// Logisim project COMBNATIONALMULTIPLIER.circ as structural Verilog: 1 circuit, main circuit MUTIPL
module MUTIPL (
  input  A0,
  input  A1,
  input  A2,
  input  B0,
  input  B1,
  input  B2,
  output S0,
  output S1,
  output S2,
  output S3,
  output S4,
  output S5
);

  wire and_2_out, and_3_out, and_4_out, and_5_out, and_6_out, and_7_out, and_8_out, and_9_out, and_10_out,
       and_11_out, and_12_out, and_13_out, and_14_out, and_15_out, and_16_out, and_17_out, and_18_out,
       or_1_out, or_3_out, xor_2_out, xor_3_out, xor_4_out, xor_5_out, xor_7_out;

  and and_1 (S0, A0, B0);
  and and_2 (and_2_out, A0, B1);
  and and_3 (and_3_out, A0, B2);
  and and_4 (and_4_out, A1, B0);
  and and_5 (and_5_out, A1, B1);
  and and_6 (and_6_out, A1, B2);
  and and_7 (and_7_out, A2, B0);
  and and_8 (and_8_out, A2, B1);
  and and_9 (and_9_out, A2, B2);
  and and_10 (and_10_out, and_5_out, and_7_out);
  xor xor_1 (S1, and_2_out, and_4_out);
  and and_11 (and_11_out, and_2_out, and_4_out);
  xor xor_2 (xor_2_out, and_5_out, and_7_out);
  and and_12 (and_12_out, and_8_out, or_1_out);
  xor xor_3 (xor_3_out, and_12_out, and_9_out);
  and and_13 (and_13_out, and_12_out, and_9_out);
  and and_14 (and_14_out, xor_2_out, and_11_out);
  xor xor_4 (xor_4_out, and_8_out, or_1_out);
  xor xor_5 (xor_5_out, xor_2_out, and_11_out);
  xor xor_6 (S4, xor_3_out, or_3_out);
  and and_15 (and_15_out, xor_3_out, or_3_out);
  or or_1 (or_1_out, and_14_out, and_10_out);
  xor xor_7 (xor_7_out, xor_4_out, and_6_out);
  and and_16 (and_16_out, xor_4_out, and_6_out);
  or or_2 (S5, and_13_out, and_15_out);
  and and_17 (and_17_out, xor_7_out, and_18_out);
  and and_18 (and_18_out, and_3_out, xor_5_out);
  xor xor_8 (S3, xor_7_out, and_18_out);
  xor xor_9 (S2, xor_5_out, and_3_out);
  or or_3 (or_3_out, and_16_out, and_17_out);

  // Notes on the sheet:
  //   A0B0
  //   A1B0
  //   A1B1
  //   A2B0
  //   A2B1
  //   A2B2
  //   A0B1
  //   A0B2
  //   A1B2
endmodule
